# Fritzing sketch Weather Station Sketch (saved by Fritzing 0.9.3b)
breadboards: 1

parts:
  Part1 = Arduino Uno (Rev3)
  DHT11 = DHT11 Humitidy and Temperature Sensor
  Water_Level_Sensor = Water Level Sensor  # not connected
  HC-SR04_ULTRASONIC_SENSOR = SRF05 Ultrasonic Rangefinder
  Vibration_Motor = Vibration Motor
  R1 = Resistor [tolerance=±5% resistance=220 package="2512 [SMD]"]
  Barometric_Pressure_Sensor_BMP180 = Barometric Pressure Sensor - BMP180 Breakout (GY-68)

nets:
  N1: Part1.D11_PWM/MOSI, Barometric_Pressure_Sensor_BMP180.SDA
  N2: Part1.D12/MISO, Barometric_Pressure_Sensor_BMP180.SCL
  N3: Part1.D3_PWM, R1.Pin_0
  N4: Part1.D4, HC-SR04_ULTRASONIC_SENSOR.Echo
  N5: Part1.D5_PWM, HC-SR04_ULTRASONIC_SENSOR.Trig
  N6: Part1.D7, DHT11.DATA
  GND: Part1.GND, DHT11.GND, HC-SR04_ULTRASONIC_SENSOR.GND, Vibration_Motor.NEG, Barometric_Pressure_Sensor_BMP180.GND
  VCC: DHT11.VDD, HC-SR04_ULTRASONIC_SENSOR.VCC, Barometric_Pressure_Sensor_BMP180.VCC
  N7: Vibration_Motor.POS, R1.Pin_1

custom parts:
  DHT11 Humitidy and Temperature Sensor: DHT11 Humidity and Temperature Sensor
  Water Level Sensor: A water level sensor. This sensor operates at 3V to 5V. The Sig (signal) pin outputs an analogue signal that is in proportion to the amount of water in contact with the sensor.
  Vibration Motor: An eccentric vibration motor!
